# Fritzing sketch Wake Up Light Perfboard (saved by Fritzing 0.9.3b)
perfboards: 1

parts:
  Part1 = Arduino Pro Mini v13
  R1 = Resistor [tolerance=±5% resistance=470 package=THT]
  C1 = Electrolytic Capacitor [capacitance=0.1nF package="100 mil [THT, electrolytic]"]  # not connected
  ZS-042_RTC1 = ZS-042 RTC Module
  ZS-042_RTC2 = ZS-042 RTC Module  # not connected
  R2 = Resistor [tolerance=±5% resistance=470 package=THT]
  J1 = Dagu DGServo 9g header (male) [package=THT]
  J2 = Dagu DGServo 9g header (male) [package=THT]  # not connected
  Power_plug1 = Power plug
  Power_plug2 = Power plug  # not connected
  Power_plug3 = Power plug  # not connected
  J3 = Dagu DGServo 9g header (male) [package=THT]  # not connected

nets:
  VCC: Part1.VCC, ZS-042_RTC1.VCC
  N1: Part1.D6_PWM, R2.Pin_1
  N2: Part1.D5_PWM, R1.Pin_1
  N3: J1.pulse, Power_plug1.GND
